# Fritzing sketch throttle-guage-pixel-panel (saved by Fritzing 1.0.4)
circuit board: 21.0382cm x 1.55021cm
breadboards: 1

parts:
  T02 = Adafruit Breadboard-Friendly NeoPixel [part_number="Adafruit #1312"]
  T03 = Adafruit Breadboard-Friendly NeoPixel [part_number="Adafruit #1312"]
  T04 = Adafruit Breadboard-Friendly NeoPixel [part_number="Adafruit #1312"]
  T05 = Adafruit Breadboard-Friendly NeoPixel [part_number="Adafruit #1312"]
  T06 = Adafruit Breadboard-Friendly NeoPixel [part_number="Adafruit #1312"]
  T07 = Adafruit Breadboard-Friendly NeoPixel [part_number="Adafruit #1312"]
  T09 = Adafruit Breadboard-Friendly NeoPixel [part_number="Adafruit #1312"]
  T10 = Adafruit Breadboard-Friendly NeoPixel [part_number="Adafruit #1312"]
  T01 = Adafruit Breadboard-Friendly NeoPixel [part_number="Adafruit #1312"]
  T11 = Adafruit Breadboard-Friendly NeoPixel [part_number="Adafruit #1312"]
  T12 = Adafruit Breadboard-Friendly NeoPixel [part_number="Adafruit #1312"]
  T13 = Adafruit Breadboard-Friendly NeoPixel [part_number="Adafruit #1312"]
  T14 = Adafruit Breadboard-Friendly NeoPixel [part_number="Adafruit #1312"]
  T15 = Adafruit Breadboard-Friendly NeoPixel [part_number="Adafruit #1312"]
  T08 = Adafruit Breadboard-Friendly NeoPixel [part_number="Adafruit #1312"]
  B01 = Adafruit Breadboard-Friendly NeoPixel [part_number="Adafruit #1312"]
  B04 = Adafruit Breadboard-Friendly NeoPixel [part_number="Adafruit #1312"]
  B02 = Adafruit Breadboard-Friendly NeoPixel [part_number="Adafruit #1312"]
  B03 = Adafruit Breadboard-Friendly NeoPixel [part_number="Adafruit #1312"]
  B05 = Adafruit Breadboard-Friendly NeoPixel [part_number="Adafruit #1312"]
  J2 = male pin header, 4 pins [form="♂ (male)"]

nets:
  N1: T02.IN, T01.OUT
  GND: T02.GND, T03.GND, T04.GND, T05.GND, T06.GND, T07.GND, T09.GND, T10.GND, T01.GND, T11.GND, T12.GND, T13.GND, T14.GND, T15.GND, T08.GND, B01.GND, B04.GND, B02.GND, B03.GND, B05.GND, J2.pin1
  VDD: T02.VDD, T03.VDD, T04.VDD, T05.VDD, T06.VDD, T07.VDD, T09.VDD, T10.VDD, T01.VDD, T11.VDD, T12.VDD, T13.VDD, T14.VDD, T15.VDD, T08.VDD, B01.VDD, B04.VDD, B02.VDD, B03.VDD, B05.VDD, J2.pin2
  N2: T02.OUT, T03.IN
  N3: T03.OUT, T04.IN
  N4: T04.OUT, T05.IN
  N5: T05.OUT, T06.IN
  N6: T06.OUT, T07.IN
  N7: T07.OUT, T08.IN
  N8: T09.IN, T08.OUT
  N9: T09.OUT, T10.IN
  N10: T10.OUT, T11.IN
  N11: T01.IN, J2.pin3
  N12: T11.OUT, T12.IN
  N13: T12.OUT, T13.IN
  N14: T13.OUT, T14.IN
  N15: T14.OUT, T15.IN
  N16: B01.IN, J2.pin4
  N17: B01.OUT, B02.IN
  N18: B04.IN, B03.OUT
  N19: B04.OUT, B05.IN
  N20: B02.OUT, B03.IN

custom parts:
  Adafruit Breadboard-Friendly NeoPixel: This is the easiest way possible to add small, bright RGB pixels to your project. We took the same technology from our Flora NeoPixels and made them breadboard friendly, with two rows of 3 x 0.1" spaced header on each side for easy soldering, chaining and breadboarding. These ultra-bright LEDs have a constant-current driver cooked right into the LED package! The pixels are chainable - so you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
